# Fritzing sketch sketch of ckt (saved by Fritzing 0.9.3b)
breadboards: 1

parts:
  Part1 = Arduino Uno (Rev3)
  Part2 = Soil Moisture Sensor
  U1 = LM393 [package=so08]
  RHT1 = Humidity and Temperature Sensor RHT03
  DS1 = DS18B20 1-Wire Temperature Sensor [part_number=DS18B20]  # not connected
  R1 = Photocell (LDR) [package=THT]
  R2 = Resistor [tolerance=±5% resistance=220 package="0402 [SMD]"]
  R3 = Resistor [tolerance=±5% resistance=220 package="2010 [SMD]"]
  Adafruit_HUZZAH_ESP8266_Breakout1 = Adafruit HUZZAH ESP8266 Breakout [part_number=2471]

nets:
  N1: Part1.A0, U1.G1_+IN
  N2: Part1.D11_PWM/MOSI, RHT1.Data-signal, R2.Pin_0
  GND: Part1.GND, U1.G1_V+, RHT1.GND_2, R1.pin_0, Adafruit_HUZZAH_ESP8266_Breakout1.GND
  N3: Part1.D5_PWM, R3.Pin_0
  N4: Part1.D6_PWM, Adafruit_HUZZAH_ESP8266_Breakout1.TX
  N5: Part1.D7, Adafruit_HUZZAH_ESP8266_Breakout1.RX
  N6: Part1.3V3, Adafruit_HUZZAH_ESP8266_Breakout1.V+
  5V: Part1.5V, U1.G1_V-, RHT1.Vcc, R2.Pin_1, R3.Pin_1
  N7: Part2.SIG, U1.G2_OUT
  N8: Part2.VCC, U1.G2_-IN
